// Logisim project brainfuck_machine.circ as structural Verilog: 2 circuits, main circuit main
module main (
  output OUTPUT_READY,
  output AWAITING_INPUT
);

  wire and_1_out, and_2_out, and_3_out, and_4_out, and_5_out, and_6_out, and_7_out, and_8_out, and_9_out,
       and_10_out, and_11_out, and_12_out, clock_1_out, clock_2_out, clock_3_out, clock_4_out, clock_5_out,
       clock_6_out, clock_7_out, clock_8_out, clock_9_out, clock_10_out, clock_11_out, clock_12_out,
       clock_13_out, clock_14_out, clock_15_out, clock_16_out, comparator_1_eq, comparator_2_eq,
       comparator_3_eq, comparator_4_eq, comparator_5_eq, comparator_6_eq, comparator_7_eq, comparator_8_eq,
       comparator_9_eq, comparator_10_eq, comparator_11_eq, controlled_buffer_10_out, d_ff_1_qn,
       EXT_RESET_out, j_k_ff_1_q, j_k_ff_2_q, j_k_ff_2_qn, j_k_ff_3_q, j_k_ff_3_qn, j_k_ff_4_qn, j_k_ff_5_q,
       j_k_ff_5_qn, monostable_1_pulse, monostable_2_pulse, nor_1_out, nor_2_out, not_1_out, not_2_out,
       not_3_out, not_4_out, or_1_out, or_2_out, or_3_out, RESET_out, STARTUP_q;
  wire [2:2] OUTPUT_CONFIRMED_out;
  wire [6:0] bit_extender_2_out, keyboard_1_data;
  wire [7:0] adder_1_out, controlled_buffer_1_out, controlled_buffer_4_out, controlled_buffer_8_out, R_IN_q,
       R_OUT_q, ram_1_data, register_1_q, register_2_q, rom_1_data, subtractor_1_out;
  wire [8:0] PUSH_INPUT_out;
  wire [14:0] adder_2_out, counter_1_q, counter_2_q, counter_3_q, Jump_Snapshot_q, ram_2_data, undriven;

  Button RESET (.out(RESET_out));
  D_Flip_Flop STARTUP (.D(1'b1), .clk(clock_1_out), .Q(STARTUP_q), .reset(RESET_out));  // open: Qn, preset
  Clock clock_1 (.out(clock_1_out));
  D_Flip_Flop d_ff_1 (.D(STARTUP_q), .clk(clock_2_out), .Qn(d_ff_1_qn), .reset(RESET_out));  // open: Q, preset
  Clock clock_2 (.out(clock_2_out));
  nor nor_1 (nor_1_out, comparator_9_eq, d_ff_1_qn, j_k_ff_2_q, AWAITING_INPUT);
  nor nor_2 (nor_2_out, d_ff_1_qn, j_k_ff_2_q, and_10_out, j_k_ff_5_q);
  Counter #(.max('h7fff), .width(15)) counter_1 (
    .clr(RESET_out), .load(and_9_out), .count(nor_1_out), .clk(clock_3_out), .D(ram_2_data), .Q(counter_1_q));  // open: up, carry
  Clock clock_3 (.out(clock_3_out));
  Counter #(.max('h7fff), .trigger("falling"), .width(15)) counter_2 (
    .clr(RESET_out), .up(comparator_1_eq), .count(and_2_out), .clk(clock_4_out), .D(undriven), .Q(counter_2_q));  // open: load, carry
  Clock clock_4 (.out(clock_4_out));
  Counter #(.max('h7fff), .trigger("falling"), .width(15)) counter_3 (
    .clr(RESET_out), .up(comparator_7_eq), .count(or_3_out), .clk(clock_5_out), .Q(counter_3_q));  // open: load, D, carry
  Clock clock_5 (.out(clock_5_out));
  Clock clock_6 (.out(clock_6_out));
  ROM #(.addrWidth(15)) rom_1 (.addr(counter_1_q), .data(rom_1_data));
  RAM #(.addrWidth(15), .asyncread("true"), .clearpin("true"), .databus("bidir"), .trigger("falling")) ram_1 (
    .addr(counter_2_q), .we(and_1_out), .oe(not_1_out), .clk(clock_6_out), .data(ram_1_data), .clr(RESET_out));
  not not_1 (not_1_out, and_1_out);
  not not_2 (not_2_out, and_8_out);
  Clock clock_7 (.out(clock_7_out));
  RAM #(.addrWidth(15), .asyncread("true"), .clearpin("true"), .dataWidth(15), .databus("bidir"), .trigger("falling")) ram_2 (
    .addr(counter_3_q), .we(and_8_out), .oe(not_2_out), .clk(clock_7_out), .data(ram_2_data), .clr(RESET_out));
  not not_3 (not_3_out, j_k_ff_5_q);
  assign controlled_buffer_1_out = j_k_ff_5_q ? {8{1'b0}} : 8'bz;  // Controlled_Buffer controlled_buffer_1
  assign controlled_buffer_1_out = not_3_out ? rom_1_data : 8'bz;  // Controlled_Buffer controlled_buffer_2
  Adder adder_1 (.a(ram_1_data), .b(8'h1), .out(adder_1_out));  // open: cin, cout
  Subtractor subtractor_1 (.a(ram_1_data), .b(8'h1), .out(subtractor_1_out));  // open: bin, bout
  assign ram_2_data = and_8_out ? counter_1_q : 15'bz;  // Controlled_Buffer controlled_buffer_3
  Comparator comparator_1 (.a(controlled_buffer_1_out), .b(8'h3e), .eq(comparator_1_eq));  // open: gt, lt
  Comparator comparator_2 (.a(controlled_buffer_1_out), .b(8'h3c), .eq(comparator_2_eq));  // open: gt, lt
  Comparator comparator_3 (.a(controlled_buffer_1_out), .b(8'h2b), .eq(comparator_3_eq));  // open: gt, lt
  Comparator comparator_4 (.a(controlled_buffer_1_out), .b(8'h2d), .eq(comparator_4_eq));  // open: gt, lt
  Comparator comparator_5 (.a(controlled_buffer_1_out), .b(8'h2e), .eq(comparator_5_eq));  // open: gt, lt
  Comparator comparator_6 (.a(controlled_buffer_1_out), .b(8'h2c), .eq(comparator_6_eq));  // open: gt, lt
  Comparator comparator_7 (.a(rom_1_data), .b(8'h5b), .eq(comparator_7_eq));  // open: gt, lt
  Comparator comparator_8 (.a(rom_1_data), .b(8'h5d), .eq(comparator_8_eq));  // open: gt, lt
  Comparator comparator_9 (.a(rom_1_data), .b({8{1'b0}}), .eq(comparator_9_eq));  // open: gt, lt
  Register register_1 (.D(adder_1_out), .clk(clock_8_out), .Q(register_1_q), .clr(RESET_out));  // open: en
  Clock clock_8 (.out(clock_8_out));
  Register register_2 (.D(subtractor_1_out), .clk(clock_9_out), .Q(register_2_q), .clr(RESET_out));  // open: en
  Clock clock_9 (.out(clock_9_out));
  assign controlled_buffer_4_out = comparator_3_eq ? register_1_q : 8'bz;  // Controlled_Buffer controlled_buffer_4
  assign controlled_buffer_4_out = comparator_4_eq ? register_2_q : 8'bz;  // Controlled_Buffer controlled_buffer_5
  or or_1 (or_1_out, comparator_3_eq, comparator_4_eq, comparator_6_eq);
  and and_1 (and_1_out, or_1_out, nor_2_out);
  assign controlled_buffer_4_out = comparator_6_eq ? R_IN_q : 8'bz;  // Controlled_Buffer controlled_buffer_6
  assign ram_1_data = and_1_out ? controlled_buffer_4_out : 8'bz;  // Controlled_Buffer controlled_buffer_7
  monostable monostable_1 (.WAVE(OUTPUT_CONFIRMED_out[2]), .PULSE(monostable_1_pulse));
  or or_2 (or_2_out, comparator_1_eq, comparator_2_eq);
  and and_2 (and_2_out, or_2_out, nor_2_out);
  and and_3 (and_3_out, j_k_ff_2_q, monostable_1_pulse);
  and and_4 (and_4_out, j_k_ff_2_q, j_k_ff_1_q);
  and and_5 (and_5_out, j_k_ff_2_qn, comparator_5_eq);
  or or_3 (or_3_out, comparator_8_eq, comparator_7_eq);
  J_K_Flip_Flop #(.trigger("falling")) j_k_ff_1 (
    .J(1'b0), .K(j_k_ff_1_q), .clk(clock_10_out), .Q(j_k_ff_1_q), .preset(and_3_out), .reset(RESET_out));  // open: Qn
  Clock clock_10 (.out(clock_10_out));
  J_K_Flip_Flop #(.trigger("falling")) j_k_ff_2 (
    .J(and_5_out), .K(and_4_out), .clk(clock_11_out), .Q(j_k_ff_2_q), .Qn(j_k_ff_2_qn), .reset(RESET_out));  // open: preset
  Clock clock_11 (.out(clock_11_out));
  Register #(.trigger("falling")) R_OUT (
    .D(ram_1_data), .en(and_5_out), .clk(clock_12_out), .Q(R_OUT_q), .clr(RESET_out));
  Clock clock_12 (.out(clock_12_out));
  Register R_IN (
    .D(controlled_buffer_8_out), .en(AWAITING_INPUT), .clk(controlled_buffer_10_out), .Q(R_IN_q),
    .clr(RESET_out));
  J_K_Flip_Flop #(.trigger("falling")) j_k_ff_3 (
    .J(1'b0), .K(and_6_out), .clk(clock_13_out), .Q(j_k_ff_3_q), .Qn(j_k_ff_3_qn),
    .preset(monostable_2_pulse), .reset(RESET_out));
  and and_6 (and_6_out, AWAITING_INPUT, j_k_ff_3_q);
  Clock clock_13 (.out(clock_13_out));
  and and_7 (and_7_out, comparator_6_eq, j_k_ff_4_qn);
  Comparator comparator_10 (.a(ram_1_data), .b({8{1'b0}}), .eq(comparator_10_eq));  // open: gt, lt
  monostable monostable_2 (.WAVE(controlled_buffer_10_out), .PULSE(monostable_2_pulse));
  J_K_Flip_Flop #(.trigger("falling")) j_k_ff_4 (
    .J(and_7_out), .K(and_6_out), .clk(clock_14_out), .Q(AWAITING_INPUT), .Qn(j_k_ff_4_qn), .reset(RESET_out));  // open: preset
  Clock clock_14 (.out(clock_14_out));
  not not_4 (not_4_out, comparator_10_eq);
  and and_8 (and_8_out, comparator_7_eq, not_4_out);
  and and_9 (and_9_out, not_4_out, comparator_8_eq);
  assign controlled_buffer_8_out = comparator_5_eq ? R_OUT_q : 8'bz;  // Controlled_Buffer controlled_buffer_8
  and and_10 (and_10_out, AWAITING_INPUT, j_k_ff_3_qn);
  and and_11 (and_11_out, j_k_ff_5_q, comparator_8_eq, comparator_11_eq);
  and and_12 (and_12_out, j_k_ff_5_qn, comparator_10_eq, comparator_7_eq);
  assign OUTPUT_READY = comparator_5_eq ? j_k_ff_2_q : 1'bz;  // Controlled_Buffer controlled_buffer_9
  J_K_Flip_Flop #(.trigger("falling")) j_k_ff_5 (
    .J(and_12_out), .K(and_11_out), .clk(clock_15_out), .Q(j_k_ff_5_q), .Qn(j_k_ff_5_qn), .reset(RESET_out));  // open: preset
  Clock clock_15 (.out(clock_15_out));
  Adder #(.width(15)) adder_2 (.a(counter_3_q), .b(15'h1), .out(adder_2_out));  // open: cin, cout
  assign controlled_buffer_10_out = AWAITING_INPUT ? OUTPUT_READY : 1'bz;  // Controlled_Buffer controlled_buffer_10
  Register #(.trigger("falling"), .width(15)) Jump_Snapshot (
    .D(adder_2_out), .en(and_12_out), .clk(clock_16_out), .Q(Jump_Snapshot_q), .clr(RESET_out));
  Clock clock_16 (.out(clock_16_out));
  Comparator #(.width(15)) comparator_11 (.a(Jump_Snapshot_q), .b(counter_3_q), .eq(comparator_11_eq));  // open: gt, lt
  Keyboard keyboard_1 (.clk(PUSH_INPUT_out[0]), .clr(EXT_RESET_out), .data(keyboard_1_data));  // open: re, avail
  assign {controlled_buffer_8_out, OUTPUT_READY} = AWAITING_INPUT ? PUSH_INPUT_out : 9'bz;  // Controlled_Buffer controlled_buffer_11
  Button PUSH_INPUT (.out(PUSH_INPUT_out[0]));
  assign PUSH_INPUT_out[8:1] = {{1{1'b0}}, keyboard_1_data};  // Bit_Extender bit_extender_1
  Button OUTPUT_CONFIRMED (.out(OUTPUT_CONFIRMED_out[2]));
  Bit_Extender #(.out_width(7), .\type ("zero")) bit_extender_2 (
    .in(controlled_buffer_8_out), .out(bit_extender_2_out));
  TTY tty_1 (.data(bit_extender_2_out), .clk(OUTPUT_CONFIRMED_out[2]), .we(OUTPUT_READY), .clr(EXT_RESET_out));
  Button EXT_RESET (.out(EXT_RESET_out));

  // Notes on the sheet:
  //   contents of rom_1 (hex, n*v repeats v):
  //   3e 2c 10*2d 5b 38*2d 3e 10*2b 3c 3c 5b 2d 3e 3e 3e 2b 3c 3c 3c 5d 3e 3e 5b 2d 3e 5b 2d 3e 2b 3c 3c d
  //   a 3c 3c 2b 3e 3e 3e 5d 3e 5b 2d 3c 2b 3e 5d 3c 3c 5d 3e 5b 2d 5d 3c 3c 5b 2d 3c 2b 3e 5d 2c 10*2d 5d
  //   2b 3c 2d 5b 2b 3e 2b 3c 5b 2d 3e 3e 2b 3e 2b 3c 3c 3c 5d 3e 3e 3e 5b 2d 3c 3c 3c 2b 3e 3e 3e 5d 3e
  //   2b 5b 5b 2d 3c 2b 3c 2d 3c 2d 5b d a 2d 4*3e 2b 3e 2b 5*3c 5d 5*3e 5b 2d 5*3c 2b 5*3e 5d 3c 5b 3c 2b
  //   3e 5b 2d 5d 5d 3c 5b 2d 3e 2b 3e 2b 3c 3c 5d 3e 3e 5b 2d 3c 3c 2b 3e 3e 5d 3c 5b 5b 2d 5d 3c 2d 3c
  //   3c 5b 2d 3e 3e 3e 2b 3e 2b 4*3c 5d 3e d a 3e 3e 3e 5b 2d 4*3c 2b 4*3e 5d 3c 5b 3c 2b 3e 5b 2d 5d 5d
  //   5d 3c 5d 3c 3c 5b 2d 3e 3e 3e 2b 3e 2b 4*3c 5d 4*3e 5b 2d 4*3c 2b 4*3e 5d 3c 5b 3c 2b 3e 5b 2d 5d 5d
  //   3c 5b 2d 3e 2b 3e 2b 3c 3c 5d 3e 3e 5b 2d 3c 3c 2b 3e d a 3e 5d 3c 5b 3c 3c 5b 2d 3c 3c 2b 3e 3e 5d
  //   3e 3e 5b 2d 5d 5d 3c 5d 2b 3c 3c 3c 5b 2d 4*3e 2b 3e 2b 5*3c 5d 5*3e 5b 2d 5*3c 2b 5*3e 5d 3c 5b 3c
  //   2d 3e 5b 2d 5d 5d 3c 3c 5b 2d 3c 3c 2b 3e 3e 5d 3e 5b 2d 3c 2b 3e d a 5d 3c 5b 2d 3c 3c 3c 5b 3e 3e
  //   2b 3c 5b 2d 3c 2d 3e 3e 3e 2b 3c 3c 5d 3e 3e 5b 2d 3c 3c 2b 3e 3e 5d 3c 3c 3c 5d 3e 3e 5b 2d 3c 3c
  //   2b 3e 3e 5d 3c 5b 2d 3e 2b 3e 2b 3c 3c 5d 3e 3e 5b 2d 3c 3c 2b 3e 3e 5d 2b 5b 3e 10*2b 5b 3c 3c 5b
  //   2d d a 3e 3e 3e 2b 3e 2b 4*3c 5d 4*3e 5b 2d 4*3c 2b 4*3e 5d 3c 5b 3c 3c 3c 2d 3e 3e 3e 5b 2d 5d 5d
  //   3c 2d 5d 3e 3e 3e 2b 4*3c 2d 5d 4*3e 5b 2d 4*3c 2b 4*3e 5d 5*3c 5b 5b 2d 5d 3e 5b 2d 3e 2b 2b 2b d a
  //   7*2b 3c 5d 3e 5b 2d 3c 2b 3e 5d 3c 3c 3c 5b 2d 3e 2b 3e 3e 2b 3c 3c 3c 5d 3e 3e 3e 5b 2d 3c 3c 3c 2b
  //   3e 3e 3e 5d 3c 5b 3e 10*2b 5b 3c 3c 5b 2d 3e 3e 3e 2b 3e 2b 4*3c 5d 4*3e 5b 2d 4*3c 2b 3e 3e d a 3e
  //   3e 5d 3c 5b 3c 3c 3c 2d 3e 3e 3e 5b 2d 5d 5d 3c 2d 5d 3e 3e 3e 2b 4*3c 2d 5d 4*3e 5b 2d 4*3c 2b 4*3e
  //   5d 5*3c 5d 3c 5b 2d 3e 2b 3e 3e 2b 3c 3c 3c 5d 3e 3e 3e 5b 2d 3c 3c 3c 2b 3e 3e 3e 5d 3c 2d 5b 2b 3e
  //   3e 3e 2b 5b d a 5b 2d 3c 3c 2b 3c 2d 3c 2d 3e 5b 2d 4*3e 2b 3e 2b 5*3c 5d 5*3e 5b 2d 5*3c 2b 5*3e 5d
  //   3c 5b 3c 2b 3e 5b 2d 5d 5d 3c 5b 2d 3e 2b 3e 2b 3c 3c 5d 3e 3e 5b 2d 3c 3c 2b 3e 3e 5d 3c 5b 5b 2d
  //   5d 3c 2d 4*3c 5b d a 2d 5*3e 2b 3e 2b 6*3c 5d 6*3e 5b 2d 6*3c 2b 6*3e 5d 3c 5b 3c 2b 3e 5b 2d 5d 5d
  //   5d 3c 5d 2b 3c 3c 3c 5b 2d 4*3e 2b 3e 2b 5*3c 5d 5*3e 5b 2d 5*3c 2b 3e 3e 3e d a 3e 3e 5d 3c 5b 5b
  //   2d 5d 3c 2d 3e 5d 3c 5b 2d 3e 2b 3e 2b 3c 3c 5d 3e 3e 5b 2d 3c 3c 2b 3e 3e 5d 3c 5b 5b 2d 5d 3c 3c
  //   2b 3c 5b 2d 3c 2b 3e 5d 3e 3e 3e 5d 3c 5d 3c 31*2b d a 17*2b 2e 5b 2d 5d 3c 5b 2d 3c 2b 3c 2b 3e 3e
  //   5d 3c 5b 10*2d 3e 2b 3c 5d 3e 5b 2d 3c 2b 3e 5d 3c 2d 5d 3c 27*2b d a 21*2b 2e 5b 2d 5d 10*2b 2e 5b
  //   2d 5d 3c 3c 5b 2d 3e 3e 2b 3e 2b 3c 3c 3c 5d 3e 3e 3e 5b 2d 3c 3c 3c 2b 3e 3e 3e 5d 3e 2b 5b 5b 2d
  //   3c 2b 3c 2d 3c 2d 5b 2d 4*3e 2b 3e 2b d a 5*3c 5d 5*3e 5b 2d 5*3c 2b 5*3e 5d 3c 5b 3c 2b 3e 5b 2d 5d
  //   5d 3c 5b 2d 3e 2b 3e 2b 3c 3c 5d 3e 3e 5b 2d 3c 3c 2b 3e 3e 5d 3c 5b 5b 2d 5d 3c 2d 3c 3c 5b 2d 3e
  //   3e 3e 2b 3e 2b 4*3c 5d 4*3e 5b 2d 3c 3c 3c d a 3c 2b 4*3e 5d 3c 5b 3c 2b 3e 5b 2d 5d 5d 5d 3c 5d 3c
  //   3c 5b 2d 3e 3e 3e 2b 3e 2b 4*3c 5d 4*3e 5b 2d 4*3c 2b 4*3e 5d 3c 5b 3c 2b 3e 5b 2d 5d 5d 3c 5b 2d 3e
  //   2b 3e 2b 3c 3c 5d 3e 3e 5b 2d 3c 3c 2b 3e 3e 5d 3c 5b 3c 3c 5b 2d d a 3c 3c 2b 3e 3e 5d 3e 3e 5b 2d
  //   5d 5d 3c 5d 2b 3c 3c 3c 5b 2d 4*3e 2b 3e 2b 5*3c 5d 5*3e 5b 2d 5*3c 2b 5*3e 5d 3c 5b 3c 2d 3e 5b 2d
  //   5d 5d 3c 3c 5b 2d 3c 3c 2b 3e 3e 5d 3e 5b 2d 3c 2b 3e 5d 3c 5d 3c 3c 3c 2d 5d
  //   >
  //   <
  //   +
  //   -
  //   .
  //   ,
  //   [
  //   ]
  //   \0
  //   State OUTPUT
  //   OE
  //   IE
  //   State INPUT
  //   State JUMPING
endmodule

module monostable (
  input  WAVE,
  output PULSE
);

  wire not_1_out;

  not not_1 (not_1_out, WAVE);
  and and_1 (PULSE, not_1_out, WAVE);
endmodule
